# Fritzing sketch ラジコン_ブレッドボード (saved by Fritzing 0.9.4)
breadboards: 1

parts:
  BAT9 = LIPO-110mAh [package=lipo-110]
  パーツ1 = Motor Driver 1A Dual TB6612FNG  # not connected
  Mod1 = Microbit
  M1 = DC Motor  # not connected
  C1 = Ceramic Capacitor [capacitance=100nF package="100 mil [THT, multilayer]"]  # not connected
  J1 = Basic Servo
  パーツ2 = Adafruit Analog 2-Axis Joystick [part_number="Adafruit #512"]
  パーツ3 = Adafruit Analog 2-Axis Joystick [part_number="Adafruit #512"]
  Mod2 = Microbit
  VCC1 = Battery  # not connected
  VCC2 = Battery

nets:
  N1: BAT9.+, J1.vcc
  GND: BAT9.-, Mod1.GND, Mod1.Bat_-, J1.gnd, VCC2.-
  N2: Mod1.P0, J1.pulse
  N3: Mod1.3V3, VCC2.+
  GND_2: パーツ2.GND, パーツ3.GND, Mod2.GND
  N4: パーツ2.XOUT, Mod2.P0
  VCC: パーツ2.VCC, パーツ3.VCC, Mod2.3V3
  N5: パーツ3.YOUT, Mod2.P1

custom parts:
  Microbit: BBC Microbit Fritzing part. May 2019 expanded to include schematic and pcb views as well as breadboard. PCB view assumes an Adafruit PRODUCT ID: 3342 2x40 Right Angle through hole edge connector (although others will probably work as well). The pcb svg is custom (see forum article http://forum.fritzing.org/t/making-edge-connectors-and-both-side-smd-parts/7287 for an explaination if you need to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
  Adafruit Analog 2-Axis Joystick: This mini-kit makes it easy to mount a PSP/Xbox-like thumb joystick to your project. The thumbstick is an analog joystick - more accurate and sensitive than just 'directional' joysticks - with a 'press in to select' button. Since it's analog, you'll need two analog reading pins on your microcontroller to determine X and Y. Having an extra digital input will let you read the switch. The pack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
