# Fritzing sketch ラジコン_基盤 (saved by Fritzing 0.9.4)
perfboards: 1

parts:
  U1 = LIPO-110mAh [package=lipo-110]
  M2 = DC Motor
  J2 = Basic Servo
  Mod3 = Microbit
  VCC3 = Battery
  JP6 = Header 2 [package=molex-1x2_lock]
  JP7 = Header 2 [package=molex-1x2_lock]
  JP16 = Header 2 [package=molex-1x2_lock]
  JP20 = Header 3 [package=molex-1x3_lock]
  JP22 = Header 3 [package=molex-1x3_lock]
  JP23 = Header 2 [package=molex-1x2_lock]
  JP24 = Header 2 [package=molex-1x2_lock]
  パーツ2 = Motor Driver 1A Dual TB6612FNG
  JP25 = Header 3 [package=molex-1x3_lock]
  JP26 = Header 3 [package=molex-1x3_lock]
  JP27 = Header 2 [package=molex-1x2_lock]  # not connected
  JP28 = Header 2 [package=molex-1x2_lock]  # not connected
  JP29 = Header 2 [package=molex-1x2_lock]
  JP30 = Header 2 [package=molex-1x2_lock]

nets:
  N1: U1.+, JP7.2
  N2: U1.-, JP7.1
  N3: M2.pin_1, JP6.1
  N4: M2.pin_2, JP6.2
  N5: J2.gnd, JP20.2
  N6: J2.vcc, JP20.1
  N7: J2.pulse, JP20.3
  N8: Mod3.P0, JP16.1
  N9: Mod3.P1, JP22.2
  N10: Mod3.P8, JP22.3
  N11: Mod3.P2, JP22.1
  N12: Mod3.3V3, JP16.2
  N13: Mod3.GND, Mod3.Bat_-, VCC3.-, JP23.2
  N14: Mod3.Bat_+, VCC3.+
  N15: JP24.1, パーツ2.GND, JP26.2
  N16: JP24.2, JP26.1
  N17: パーツ2.A02, JP30.2
  N18: パーツ2.A01, JP30.1
  N19: パーツ2.VCC, パーツ2.STBY, JP29.2
  N20: パーツ2.PWMA, JP25.3
  N21: パーツ2.AIN2, JP25.2
  N22: パーツ2.AIN1, JP25.1
  N23: JP26.3, JP29.1

custom parts:
  Microbit: BBC Microbit Fritzing part. May 2019 expanded to include schematic and pcb views as well as breadboard. PCB view assumes an Adafruit PRODUCT ID: 3342 2x40 Right Angle through hole edge connector (although others will probably work as well). The pcb svg is custom (see forum article http://forum.fritzing.org/t/making-edge-connectors-and-both-side-smd-parts/7287 for an explaination if you need to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
